// Logisim project cpu.circ as structural Verilog: 6 circuits, main circuit main
module main (
  input  [31:0] INSTRUCTION,
  input  CLOCK,
  output [31:0] FETCH_ADDRESS,
  output [31:0] s0_Value,
  output [31:0] s1_Value,
  output [31:0] t0_Value,
  output [31:0] t1_Value,
  output [31:0] a0_Value,
  output [31:0] ra_Value,
  output [31:0] sp_Value
);

  wire ASel, BrEq, BrLt, BrUn, BSel, comparator_1_eq, MEM_p1, MEM_p3, MEM_p8, MEM_p10, MEM_p14, MEM_p15,
       MEM_p18, MEM_p20, MemRW, PCSel, RegWEn;
  wire [1:0] WBSel;
  wire [2:0] funct3, ImmSel;
  wire [3:0] ALUSel;
  wire [6:0] funct7;
  wire [24:0] IMMB;
  wire [31:0] adder_2_out, alu, IMMGENOUT, INSTRUCTIONF, MEM_p13, mempayload_1_payload, multiplexer_1_out,
       multiplexer_2_out, multiplexer_4_out, multiplexer_5_out, multiplier_1_out, PC_4, PCX, R1, R2,
       shifter_1_out, shifter_2_out, wb;

  Multiplexer #(.width(32), .disabled(0), .enable("false")) multiplexer_1 (
    .in0(PC_4), .in1(multiplexer_2_out), .out(multiplexer_1_out), .sel(PCSel));
  // Probe on multiplexer_2_out
  Register #(.width(32)) PC (.D(multiplexer_1_out), .Q(FETCH_ADDRESS), .clk(CLOCK));  // open: en, clr
  Shifter #(.width(32), .shift("ar")) shifter_1 (.in(alu), .\dist (5'b00010), .out(shifter_1_out));
  Adder #(.width(32)) adder_1 (.a(32'h1), .b(FETCH_ADDRESS), .out(PC_4));  // open: cin, cout
  // Probe on INSTRUCTION
  Multiplexer #(.width(32), .enable("false")) multiplexer_2 (
    .in0(alu), .in1(shifter_1_out), .out(multiplexer_2_out), .sel(comparator_1_eq));
  Comparator #(.width(7)) comparator_1 (.a(IMMB[6:0]), .b(7'b1100111), .eq(comparator_1_eq));  // open: gt, lt
  // Probe on INSTRUCTIONF
  Multiplexer #(.width(32), .enable("false")) multiplexer_3 (
    .in0(INSTRUCTION), .in1({32{1'b0}}), .out(INSTRUCTIONF), .sel(PCSel));
  Register #(.width(32)) u_PCX (.D(FETCH_ADDRESS), .Q(PCX), .clk(CLOCK));  // open: en, clr
  Register #(.width(32)) InstrX (
    .D(INSTRUCTIONF), .Q({funct7, IMMB[24:15], funct3, IMMB[11:0]}), .clk(CLOCK));  // open: en, clr
  ImmGen immgen_1 (.INSTRUCTION({funct7, IMMB[24:15], funct3, IMMB[11:0]}), .ImmSel(ImmSel), .IMMGENOUT(IMMGENOUT));
  Control control_1 (
    .Opcode(IMMB[6:0]), .Funct3(funct3), .Funct7(funct7), .BrEq(BrEq), .BrLt(BrLt), .PCSel(PCSel),
    .ImmSel(ImmSel), .RegWEn(RegWEn), .BrUn(BrUn), .BSel(BSel), .ASel(ASel), .ALUSel(ALUSel), .MemRW(MemRW),
    .WBSel(WBSel));
  // Probe on {funct7, IMMB[24:15], funct3, IMMB[11:0]}
  regfile_main main_1 (
    .Read_Register_1__rs1(IMMB[19:15]), .Read_Register_2__rs2(IMMB[24:20]), .Write_Register__rd(IMMB[11:7]),
    .Write_Data(wb), .Write_Enable(RegWEn), .Clock(CLOCK), .Read_Data_1(R1), .Read_Data_2(R2),
    .s1_Value(s1_Value), .t0_Value(t0_Value), .t1_Value(t1_Value), .a0_Value(a0_Value), .s0_Value(s0_Value),
    .ra_Value(ra_Value), .sp_Value(sp_Value));
  // Probe on R2
  BranchComp branchcomp_1 (.R_RS1(R1), .R_RS2(R2), .BrUn(BrUn), .BrEq(BrEq), .BrLt(BrLt));
  // Probe on s0_Value
  // Probe on R1
  Multiplexer #(.width(32), .disabled(0), .enable("false")) multiplexer_4 (
    .in0(R1), .in1(PCX), .out(multiplexer_4_out), .sel(ASel));
  alu_main main_2 (.Switch(ALUSel), .X(multiplexer_4_out), .Result(alu), .Y(multiplexer_5_out));  // open: Equal
  Multiplexer #(.width(32), .disabled(0), .enable("false")) multiplexer_5 (
    .in0(R2), .in1(IMMGENOUT), .out(multiplexer_5_out), .sel(BSel));
  // Probe on multiplexer_5_out
  // Probe on s1_Value
  // Probe on alu
  // Probe on multiplexer_4_out
  Adder #(.width(32)) adder_2 (.a(PCX), .b(32'h1), .out(adder_2_out));  // open: cin, cout
  // Probe on t0_Value
  // Probe on shifter_2_out
  Shifter #(.width(32), .shift("lr")) shifter_2 (.in(alu), .\dist (5'b00010), .out(shifter_2_out));
  // Probe on alu
  Multiplier #(.width(32)) multiplier_1 (.a(adder_2_out), .b(32'h4), .out(multiplier_1_out));  // open: cin, cout
  // Probe on t1_Value
  // Probe on MEM_p13
  // mem_main MEM: pin names not known; wires that end beside it: MEM_p1, MEM_p1, MEM_p3, MEM_p3, shifter_2_out, R2, MemRW, MEM_p8, CLOCK, MEM_p10, MEM_p8, MEM_p10, MEM_p13, MEM_p14, MEM_p15, MEM_p14, MEM_p15, MEM_p18, MEM_p18, MEM_p20
  // Probe on a0_Value
  // Probe on MEM_p14
  // Probe on ra_Value
  MemPayload mempayload_1 (.Memory(MEM_p13), .Imm(IMMGENOUT), .func3(funct3), .Payload(mempayload_1_payload));
  // Probe on multiplier_1_out
  // Probe on sp_Value
  // Probe on mempayload_1_payload
  // Probe on wb
  Multiplexer #(.select(2), .width(32), .enable("false")) multiplexer_6 (
    .in0(mempayload_1_payload), .in1(alu), .in2(multiplier_1_out), .out(wb), .sel(WBSel));  // open: in3
  // Probe on WBSel

  // Other names for the same wires on the sheet: a0[31:0] = a0_Value; clk = CLOCK; fetch_addr[31:0] = FETCH_ADDRESS;
  //   PC[31:0] = FETCH_ADDRESS; INSTRUCTIONX[31:0] = {funct7, IMMB[24:15], funct3, IMMB[11:0]};
  //   opcode[6:0] = IMMB[6:0]; RW[4:0] = IMMB[11:7]; IMMB (some bits) = {funct7, funct3}; RR1[4:0] = IMMB[19:15];
  //   RR2[4:0] = IMMB[24:20]; ra[31:0] = ra_Value; s0[31:0] = s0_Value; s1[31:0] = s1_Value; sp[31:0] = sp_Value;
  //   t0[31:0] = t0_Value; t1[31:0] = t1_Value

  // Notes on the sheet:
  //   Output
  //   These are outputs/inputs from run.circ
  //   Inputs
  //   These are DEBUG/TEST outputs from your circuit.
endmodule

module BranchComp (
  input  [31:0] R_RS1,
  input  [31:0] R_RS2,
  input  BrUn,
  output BrEq,
  output BrLt
);

  wire comparator_1_lt, comparator_2_lt;

  Comparator #(.width(32)) comparator_1 (.a(R_RS1), .b(R_RS2), .eq(BrEq), .lt(comparator_1_lt));  // open: gt
  Comparator #(.width(32), .mode("unsigned")) comparator_2 (
    .a(R_RS1), .b(R_RS2), .lt(comparator_2_lt));  // open: gt, eq
  Multiplexer #(.enable("false")) multiplexer_1 (.in0(comparator_1_lt), .in1(comparator_2_lt), .out(BrLt), .sel(BrUn));
endmodule

module Control (
  input  [6:0] Opcode,
  input  [2:0] Funct3,
  input  [6:0] Funct7,
  input  BrEq,
  input  BrLt,
  output PCSel,
  output [2:0] ImmSel,
  output RegWEn,
  output BrUn,
  output BSel,
  output ASel,
  output [3:0] ALUSel,
  output MemRW,
  output [1:0] WBSel
);

  wire _00func7, _01func7, _20func7, ADD, ADDI, AND, and_1_out, and_2_out, and_3_out, and_4_out, and_5_out,
       and_7_out, and_8_out, and_15_out, and_17_out, and_25_out, and_26_out, and_27_out, and_28_out,
       and_29_out, ANDI, BEQ, BLT, comparator_13_eq, comparator_14_eq, comparator_15_eq, comparator_16_eq,
       comparator_17_eq, comparator_18_eq, comparator_19_eq, comparator_20_eq, comparator_21_eq,
       comparator_22_eq, comparator_23_eq, comparator_24_eq, comparator_25_eq, comparator_26_eq,
       comparator_27_eq, comparator_28_eq, comparator_29_eq, comparator_30_eq, comparator_31_eq,
       comparator_32_eq, comparator_33_eq, comparator_34_eq, comparator_35_eq, comparator_36_eq,
       comparator_37_eq, comparator_38_eq, comparator_39_eq, DIV, iop03, iop13, iop67, isBranch, isJump,
       ITYPE, JALR, LB, LH, LW, MUL, MULH, OR, or_3_out, or_5_out, or_6_out, or_8_out, or_10_out, or_11_out,
       or_12_out, or_14_out, or_15_out, or_16_out, ORI, REM, rop1, sbop, SLL, SLLI, SLT, SLTI, sop, SRL,
       SRLI, SUB, SW, ujop, uop, XOR, XORI;
  wire [1:0] multiplexer_10_out;
  wire [2:0] multiplexer_2_out, multiplexer_3_out, multiplexer_4_out;
  wire [3:0] multiplexer_1_out, multiplexer_5_out, multiplexer_7_out, multiplexer_8_out, multiplexer_9_out,
       multiplexer_12_out, multiplexer_13_out, multiplexer_14_out, multiplexer_15_out, multiplexer_16_out,
       multiplexer_17_out;

  Multiplexer #(.width(4), .enable("false")) multiplexer_1 (
    .in0(4'b1100), .in1(4'b1011), .out(multiplexer_1_out), .sel(uop));
  Comparator #(.width(7), .mode("unsigned")) comparator_1 (.a(Opcode), .b(7'b1100111), .eq(iop67));  // open: gt, lt
  Comparator #(.width(7), .mode("unsigned")) comparator_2 (.a(Opcode), .b(7'b1101111), .eq(ujop));  // open: gt, lt
  Comparator #(.width(7), .mode("unsigned")) comparator_3 (.a(Opcode), .b(7'b0110111), .eq(uop));  // open: gt, lt
  Comparator #(.width(7), .mode("unsigned")) comparator_4 (.a(Opcode), .b(7'b1100011), .eq(sbop));  // open: gt, lt
  Comparator #(.width(7), .mode("unsigned")) comparator_5 (.a(Opcode), .b(7'b0100011), .eq(sop));  // open: gt, lt
  Comparator #(.width(7), .mode("unsigned")) comparator_6 (.a(Opcode), .b(7'b0010011), .eq(iop13));  // open: gt, lt
  Comparator #(.width(7), .mode("unsigned")) comparator_7 (.a(Opcode), .b(7'b0000011), .eq(iop03));  // open: gt, lt
  Comparator #(.width(7), .mode("unsigned")) comparator_8 (.a(Opcode), .b(7'b0110011), .eq(rop1));  // open: gt, lt
  Comparator #(.width(7), .mode("unsigned")) comparator_9 (.a(Funct7), .b({7{1'b0}}), .eq(_00func7));  // open: gt, lt
  Comparator #(.width(7), .mode("unsigned")) comparator_10 (.a(Funct7), .b(7'b0000001), .eq(_01func7));  // open: gt, lt
  Comparator #(.width(7), .mode("unsigned")) comparator_11 (.a(Funct7), .b(7'b0100000), .eq(_20func7));  // open: gt, lt
  or or_1 (ITYPE, iop03, iop67, iop13);
  Comparator #(.width(7)) comparator_12 (.a(Opcode), .b(7'b0100011), .eq(MemRW));  // open: gt, lt
  Multiplexer #(.width(3), .enable("false")) multiplexer_2 (
    .in0(3'b100), .in1(3'b011), .out(multiplexer_2_out), .sel(uop));
  Multiplexer #(.width(3), .enable("false")) multiplexer_3 (
    .in0(multiplexer_2_out), .in1(3'b010), .out(multiplexer_3_out), .sel(sbop));
  or or_2 (RegWEn, rop1, ITYPE, uop, ujop);
  Multiplexer #(.width(3), .enable("false")) multiplexer_4 (
    .in0(multiplexer_3_out), .in1(3'b001), .out(multiplexer_4_out), .sel(sop));
  Multiplexer #(.width(4), .enable("false")) multiplexer_5 (
    .in0(multiplexer_1_out), .in1(4'b1010), .out(multiplexer_5_out), .sel(REM));
  or or_3 (or_3_out, BLT, BrUn);
  Multiplexer #(.width(3), .enable("false")) multiplexer_6 (
    .in0(multiplexer_4_out), .in1(3'b000), .out(ImmSel), .sel(ITYPE));
  Multiplexer #(.width(4), .enable("false")) multiplexer_7 (
    .in0(multiplexer_8_out), .in1(4'b1000), .out(multiplexer_7_out), .sel(MULH));
  Multiplexer #(.width(4), .enable("false")) multiplexer_8 (
    .in0(multiplexer_5_out), .in1(4'b1001), .out(multiplexer_8_out), .sel(DIV));
  Comparator #(.width(3), .mode("unsigned")) comparator_13 (
    .a(Funct3), .b(3'b000), .eq(comparator_13_eq));  // open: gt, lt
  Comparator #(.width(3), .mode("unsigned")) comparator_14 (
    .a(Funct3), .b(3'b101), .eq(comparator_14_eq));  // open: gt, lt
  Comparator #(.width(3), .mode("unsigned")) comparator_15 (
    .a(Funct3), .b(3'b110), .eq(comparator_15_eq));  // open: gt, lt
  Comparator #(.width(3), .mode("unsigned")) comparator_16 (
    .a(Funct3), .b(3'b000), .eq(comparator_16_eq));  // open: gt, lt
  Comparator #(.width(3), .mode("unsigned")) comparator_17 (
    .a(Funct3), .b(3'b001), .eq(comparator_17_eq));  // open: gt, lt
  Comparator #(.width(3), .mode("unsigned")) comparator_18 (
    .a(Funct3), .b(3'b101), .eq(comparator_18_eq));  // open: gt, lt
  Comparator #(.width(3), .mode("unsigned")) comparator_19 (
    .a(Funct3), .b(3'b010), .eq(comparator_19_eq));  // open: gt, lt
  Comparator #(.width(3), .mode("unsigned")) comparator_20 (
    .a(Funct3), .b(3'b000), .eq(comparator_20_eq));  // open: gt, lt
  Comparator #(.width(3), .mode("unsigned")) comparator_21 (
    .a(Funct3), .b(3'b110), .eq(comparator_21_eq));  // open: gt, lt
  and and_1 (and_1_out, BrEq, isBranch, BEQ);
  and and_2 (and_2_out, BrLt, isBranch, or_3_out);
  Multiplexer #(.width(4), .enable("false")) multiplexer_9 (
    .in0(multiplexer_7_out), .in1(4'b0111), .out(multiplexer_9_out), .sel(MUL));
  Comparator #(.width(3), .mode("unsigned")) comparator_22 (
    .a(Funct3), .b(3'b111), .eq(comparator_22_eq));  // open: gt, lt
  Comparator #(.width(3), .mode("unsigned")) comparator_23 (
    .a(Funct3), .b(3'b010), .eq(comparator_23_eq));  // open: gt, lt
  Comparator #(.width(3), .mode("unsigned")) comparator_24 (
    .a(Funct3), .b(3'b000), .eq(comparator_24_eq));  // open: gt, lt
  Comparator #(.width(3), .mode("unsigned")) comparator_25 (
    .a(Funct3), .b(3'b000), .eq(comparator_25_eq));  // open: gt, lt
  and and_3 (and_3_out, comparator_13_eq, _20func7);
  and and_4 (and_4_out, comparator_14_eq, _00func7);
  and and_5 (and_5_out, comparator_15_eq, _01func7);
  and and_6 (ADDI, iop13, comparator_16_eq);
  and and_7 (and_7_out, comparator_17_eq, _00func7);
  and and_8 (and_8_out, comparator_18_eq, _00func7);
  and and_9 (SW, sop, comparator_19_eq);
  and and_10 (BEQ, sbop, comparator_20_eq);
  and and_11 (BrUn, sbop, comparator_21_eq);
  not not_1 (BSel, rop1);
  or or_4 (PCSel, and_1_out, and_2_out, isJump);
  Multiplexer #(.width(2), .enable("false")) multiplexer_10 (
    .in0(2'b00), .in1(2'b10), .out(multiplexer_10_out), .sel(isJump));
  Multiplexer #(.width(2), .enable("false")) multiplexer_11 (
    .in0(multiplexer_10_out), .in1(2'b01), .out(WBSel), .sel(or_5_out));
  or or_5 (or_5_out, rop1, uop, 1'b0, iop13);
  or or_6 (or_6_out, SLT, SLTI);
  and and_12 (AND, rop1, comparator_22_eq);
  and and_13 (SLT, rop1, comparator_23_eq);
  and and_14 (ADD, rop1, and_15_out);
  and and_15 (and_15_out, comparator_24_eq, _00func7);
  and and_16 (MUL, rop1, and_17_out);
  and and_17 (and_17_out, comparator_25_eq, _01func7);
  and and_18 (SUB, rop1, and_3_out);
  and and_19 (SRL, rop1, and_4_out);
  and and_20 (REM, rop1, and_5_out);
  and and_21 (SLLI, iop13, and_7_out);
  and and_22 (SRLI, iop13, and_8_out);
  Multiplexer #(.width(4), .enable("false")) multiplexer_12 (
    .in0(multiplexer_9_out), .in1(4'b0110), .out(multiplexer_12_out), .sel(or_6_out));
  Comparator #(.width(3), .mode("unsigned")) comparator_26 (
    .a(Funct3), .b(3'b000), .eq(comparator_26_eq));  // open: gt, lt
  or or_7 (isBranch, BEQ, BLT, BrUn);
  // AND_Gate and_23 has open pins: in0=sbop, in1=or_11_out, out=open
  Multiplexer #(.width(4), .enable("false")) multiplexer_13 (
    .in0(multiplexer_12_out), .in1(4'b0101), .out(multiplexer_13_out), .sel(or_8_out));
  or or_8 (or_8_out, XOR, XORI);
  Comparator #(.width(3), .mode("unsigned")) comparator_27 (
    .a(Funct3), .b(3'b001), .eq(comparator_27_eq));  // open: gt, lt
  Comparator #(.width(3), .mode("unsigned")) comparator_28 (
    .a(Funct3), .b(3'b001), .eq(comparator_28_eq));  // open: gt, lt
  Comparator #(.width(3), .mode("unsigned")) comparator_29 (
    .a(Funct3), .b(3'b100), .eq(comparator_29_eq));  // open: gt, lt
  Comparator #(.width(3), .mode("unsigned")) comparator_30 (
    .a(Funct3), .b(3'b100), .eq(comparator_30_eq));  // open: gt, lt
  Comparator #(.width(3), .mode("unsigned")) comparator_31 (
    .a(Funct3), .b(3'b110), .eq(comparator_31_eq));  // open: gt, lt
  Comparator #(.width(3), .mode("unsigned")) comparator_32 (
    .a(Funct3), .b(3'b000), .eq(comparator_32_eq));  // open: gt, lt
  Comparator #(.width(3), .mode("unsigned")) comparator_33 (
    .a(Funct3), .b(3'b001), .eq(comparator_33_eq));  // open: gt, lt
  Comparator #(.width(3), .mode("unsigned")) comparator_34 (
    .a(Funct3), .b(3'b010), .eq(comparator_34_eq));  // open: gt, lt
  Comparator #(.width(3), .mode("unsigned")) comparator_35 (
    .a(Funct3), .b(3'b100), .eq(comparator_35_eq));  // open: gt, lt
  Comparator #(.width(3), .mode("unsigned")) comparator_36 (
    .a(Funct3), .b(3'b110), .eq(comparator_36_eq));  // open: gt, lt
  Comparator #(.width(3), .mode("unsigned")) comparator_37 (
    .a(Funct3), .b(3'b111), .eq(comparator_37_eq));  // open: gt, lt
  Comparator #(.width(3), .mode("unsigned")) comparator_38 (
    .a(Funct3), .b(3'b100), .eq(comparator_38_eq));  // open: gt, lt
  and and_24 (JALR, iop67, comparator_26_eq);
  or or_9 (ASel, isBranch, ujop);
  Multiplexer #(.width(4), .enable("false")) multiplexer_14 (
    .in0(multiplexer_13_out), .in1(4'b0100), .out(multiplexer_14_out), .sel(or_10_out));
  or or_10 (or_10_out, OR, ORI);
  and and_25 (and_25_out, comparator_27_eq, _00func7);
  and and_26 (and_26_out, comparator_28_eq, _01func7);
  and and_27 (and_27_out, comparator_29_eq, _00func7);
  and and_28 (and_28_out, comparator_30_eq, _01func7);
  and and_29 (and_29_out, comparator_31_eq, _00func7);
  and and_30 (LB, iop03, comparator_32_eq);
  and and_31 (LH, iop03, comparator_33_eq);
  Comparator #(.width(3), .mode("unsigned")) comparator_39 (
    .a(Funct3), .b(3'b010), .eq(comparator_39_eq));  // open: gt, lt
  and and_32 (SLTI, iop13, comparator_34_eq);
  and and_33 (XORI, iop13, comparator_35_eq);
  and and_34 (ORI, iop13, comparator_36_eq);
  and and_35 (ANDI, iop13, comparator_37_eq);
  and and_36 (BLT, sbop, comparator_38_eq);
  or or_11 (or_11_out, BrLt, BrEq);
  Multiplexer #(.width(4), .enable("false")) multiplexer_15 (
    .in0(multiplexer_14_out), .in1(4'b0011), .out(multiplexer_15_out), .sel(or_12_out));
  or or_12 (or_12_out, AND, ANDI);
  and and_37 (SLL, rop1, and_25_out);
  and and_38 (MULH, rop1, and_26_out);
  and and_39 (XOR, rop1, and_27_out);
  and and_40 (DIV, rop1, and_28_out);
  and and_41 (OR, rop1, and_29_out);
  and and_42 (LW, iop03, comparator_39_eq);
  or or_13 (isJump, ujop, JALR);
  or or_14 (or_14_out, ADDI, ADD, isJump, iop03, sop, isBranch);
  Multiplexer #(.width(4), .enable("false")) multiplexer_16 (
    .in0(multiplexer_15_out), .in1(4'b0010), .out(multiplexer_16_out), .sel(or_14_out));
  or or_15 (or_15_out, SRL, SRLI);
  Multiplexer #(.width(4), .enable("false")) multiplexer_17 (
    .in0(multiplexer_16_out), .in1(4'b0001), .out(multiplexer_17_out), .sel(or_15_out));
  Multiplexer #(.width(4), .enable("false")) multiplexer_18 (
    .in0(multiplexer_17_out), .in1(4'b0000), .out(ALUSel), .sel(or_16_out));
  or or_16 (or_16_out, SLL, SLLI);

  // Other names for the same wires on the sheet: BLTU = BrUn; func3[2:0] = Funct3; func7[6:0] = Funct7;
  //   op[6:0] = Opcode; RTYPE = rop1; SBTYPE = sbop; STYPE = sop; UJTYPE = ujop; UTYPE = uop
endmodule

module ImmGen (
  input  [31:0] INSTRUCTION,
  input  [2:0] ImmSel,
  output [31:0] IMMGENOUT
);

  wire [12:0] shifter_1_out;
  wire [20:0] shifter_2_out;
  wire [31:0] bit_extender_1_out, bit_extender_2_out, bit_extender_3_out, bit_extender_4_out;

  // Probe on INSTRUCTION[31:20]
  // Probe on {INSTRUCTION[31:25], INSTRUCTION[11:7]}
  // Probe on {INSTRUCTION[31], INSTRUCTION[7], INSTRUCTION[30:25], INSTRUCTION[11:8], 1'b0}
  // Probe on {INSTRUCTION[31:12], {12{1'b0}}}
  // Probe on {INSTRUCTION[31], INSTRUCTION[19:12], INSTRUCTION[20], INSTRUCTION[30:21], 1'b0}
  Shifter #(.width(13), .shift("ar")) shifter_1 (
    .in({INSTRUCTION[31], INSTRUCTION[7], INSTRUCTION[30:25], INSTRUCTION[11:8], 1'b0}), .\dist (4'b0010),
    .out(shifter_1_out));
  Shifter #(.width(21), .shift("ar")) shifter_2 (
    .in({INSTRUCTION[31], INSTRUCTION[19:12], INSTRUCTION[20], INSTRUCTION[30:21], 1'b0}), .\dist (5'b00010),
    .out(shifter_2_out));
  // Probe on shifter_2_out
  // Probe on IMMGENOUT
  assign bit_extender_1_out = {{20{INSTRUCTION[31]}}, INSTRUCTION[31:20]};  // Bit_Extender bit_extender_1
  assign bit_extender_2_out = {{20{INSTRUCTION[31]}}, {INSTRUCTION[31:25], INSTRUCTION[11:7]}};  // Bit_Extender bit_extender_2
  assign bit_extender_3_out = {{19{shifter_1_out[12]}}, shifter_1_out};  // Bit_Extender bit_extender_3
  assign bit_extender_4_out = {{11{shifter_2_out[20]}}, shifter_2_out};  // Bit_Extender bit_extender_4
  Multiplexer #(.select(3), .width(32), .enable("false")) multiplexer_1 (
    .in0(bit_extender_1_out), .in1(bit_extender_2_out), .in2(bit_extender_3_out),
    .in3({INSTRUCTION[31:12], {12{1'b0}}}), .in4(bit_extender_4_out), .out(IMMGENOUT), .sel(ImmSel));  // open: in5, in6, in7
  // Probe on ImmSel

  // Other names for the same wires on the sheet: INSTR[31:0] = INSTRUCTION; _12_31[19:0] = INSTRUCTION[31:12];
  //   _20_31[11:0] = INSTRUCTION[31:20]; _21_30[9:0] = INSTRUCTION[30:21]; ITYPEIMM[11:0] = INSTRUCTION[31:20];
  //   JTYPEIMM[20:1] = {INSTRUCTION[31], INSTRUCTION[19:12], INSTRUCTION[20], INSTRUCTION[30:21]};
  //   UTYPEIMM[31:12] = INSTRUCTION[31:12]; _25_30[5:0] = INSTRUCTION[30:25]; _25_31[6:0] = INSTRUCTION[31:25];
  //   SBTYPEIMM[12:1] = {INSTRUCTION[31], INSTRUCTION[7], INSTRUCTION[30:25], INSTRUCTION[11:8]};
  //   STYPEIMM[11:0] = {INSTRUCTION[31:25], INSTRUCTION[11:7]}; _20 = INSTRUCTION[20];
  //   _12_19[7:0] = INSTRUCTION[19:12]; _31 = INSTRUCTION[31]; _7_11[4:0] = INSTRUCTION[11:7];
  //   _8_11[3:0] = INSTRUCTION[11:8]; _7 = INSTRUCTION[7]
endmodule

module MemPayload (
  input  [31:0] Memory,
  input  [31:0] Imm,
  input  [2:0] func3,
  output [31:0] Payload
);

  wire [1:0] modulus;
  wire [7:0] multiplexer_2_out;
  wire [15:0] multiplexer_1_out;
  wire [31:0] bit_extender_2_out, bit_extender_3_out, divider_1_rem;

  Divider #(.width(32)) divider_1 (.a(Imm), .b(32'h4), .rem(divider_1_rem));  // open: out, upper
  Bit_Extender #(.in_width(32), .out_width(2)) bit_extender_1 (.in(divider_1_rem), .out(modulus));
  Multiplexer #(.select(2), .width(16), .enable("false")) multiplexer_1 (
    .in0(Memory[15:0]), .in2(Memory[31:16]), .out(multiplexer_1_out), .sel(modulus));  // open: in1, in3
  Multiplexer #(.select(2), .width(8), .enable("false")) multiplexer_2 (
    .in0(Memory[7:0]), .in1(Memory[15:8]), .in2(Memory[23:16]), .in3(Memory[31:24]), .out(multiplexer_2_out),
    .sel(modulus));
  assign bit_extender_2_out = {{16{multiplexer_1_out[15]}}, multiplexer_1_out};  // Bit_Extender bit_extender_2
  assign bit_extender_3_out = {{24{multiplexer_2_out[7]}}, multiplexer_2_out};  // Bit_Extender bit_extender_3
  Multiplexer #(.select(3), .width(32), .enable("false")) multiplexer_3 (
    .in0(bit_extender_3_out), .in1(bit_extender_2_out), .in2(Memory), .out(Payload), .sel(func3));  // open: in3, in4, in5, in6, in7

  // Other names for the same wires on the sheet: b0[7:0] = Memory[7:0]; low[15:0] = Memory[15:0];
  //   b1[7:0] = Memory[15:8]; b2[7:0] = Memory[23:16]; high[15:0] = Memory[31:16]; b3[7:0] = Memory[31:24]
endmodule

module Boundary (
  input  [31:0] Addr,
  output [31:0] Addr_Out
);

  wire [31:0] divider_1_rem;

  Divider #(.width(32)) divider_1 (.a(Addr), .b(32'h4), .rem(divider_1_rem));  // open: out, upper
  Subtractor #(.width(32)) subtractor_1 (.a(Addr), .b(divider_1_rem), .out(Addr_Out));  // open: bin, bout
endmodule
