// Logisim project cpukushal.circ as structural Verilog: 2 circuits, main circuit main
module main (
  input  [31:0] INSTRUCTION,
  input  CLOCK,
  output [31:0] FETCH_ADDRESS,
  output [31:0] s0_Value,
  output [31:0] s1_Value,
  output [31:0] t0_Value,
  output [31:0] t1_Value,
  output [31:0] a0_Value,
  output [31:0] ra_Value,
  output [31:0] sp_Value
);

  wire MEM_p1, MEM_p3, MEM_p6, MEM_p9, MEM_p12;

  Register #(.width(32)) PC ();  // open: D, en, Q, clk, clr
  // regfile_main main_1: pin names not known
  // alu_main main_2: pin names not known
  // mem_main MEM: pin names not known; wires that end beside it: MEM_p1, s0_Value, MEM_p3, MEM_p3, s1_Value, MEM_p6, MEM_p6, t0_Value, MEM_p9, MEM_p9, t1_Value, MEM_p12, MEM_p12, a0_Value

  // Other names for the same wires on the sheet: clk = CLOCK; fetch_addr[31:0] = FETCH_ADDRESS

  // Notes on the sheet:
  //   Output
  //   These are outputs/inputs from run.circ
  //   Inputs
  //   These are DEBUG/TEST outputs from your circuit.
endmodule

module control (
  input  [6:0] Opcode,
  input  [2:0] Funct3,
  input  [6:0] Funct7
);

  wire _00func7, _01func7, _20func7, ADD, ADDI, AND, and_1_out, and_2_out, and_3_out, and_4_out, and_5_out,
       and_7_out, and_8_out, and_15_out, and_17_out, and_24_out, and_25_out, and_26_out, and_27_out,
       and_28_out, ANDI, ASel, BEQ, BLT, BLTU, BrEq, BrLt, BSel, comparator_13_eq, comparator_14_eq,
       comparator_15_eq, comparator_16_eq, comparator_17_eq, comparator_18_eq, comparator_19_eq,
       comparator_20_eq, comparator_21_eq, comparator_22_eq, comparator_23_eq, comparator_24_eq,
       comparator_25_eq, comparator_26_eq, comparator_27_eq, comparator_28_eq, comparator_29_eq,
       comparator_30_eq, comparator_31_eq, comparator_32_eq, comparator_33_eq, comparator_34_eq,
       comparator_35_eq, comparator_36_eq, comparator_37_eq, comparator_38_eq, comparator_39_eq, DIV, iop03,
       iop13, iop67, isBranch, isJump, ITYPE, JALR, LB, LH, LW, MemRW, MUL, MULH, OR, or_3_out, ORI, PCSel,
       RegWEn, REM, rop1, sbop, SLL, SLLI, SLT, SLTI, sop, SRL, SRLI, SUB, SW, ujop, uop, XOR, XORI;

  Comparator #(.width(7), .mode("unsigned")) comparator_1 (.a(Opcode), .b(7'b1100111), .eq(iop67));  // open: gt, lt
  Comparator #(.width(7), .mode("unsigned")) comparator_2 (.a(Opcode), .b(7'b1101111), .eq(ujop));  // open: gt, lt
  Comparator #(.width(7), .mode("unsigned")) comparator_3 (.a(Opcode), .b(7'b0110111), .eq(uop));  // open: gt, lt
  Comparator #(.width(7), .mode("unsigned")) comparator_4 (.a(Opcode), .b(7'b1100011), .eq(sbop));  // open: gt, lt
  Comparator #(.width(7), .mode("unsigned")) comparator_5 (.a(Opcode), .b(7'b0100011), .eq(sop));  // open: gt, lt
  Comparator #(.width(7), .mode("unsigned")) comparator_6 (.a(Opcode), .b(7'b0010011), .eq(iop13));  // open: gt, lt
  Comparator #(.width(7), .mode("unsigned")) comparator_7 (.a(Opcode), .b(7'b0000011), .eq(iop03));  // open: gt, lt
  Comparator #(.width(7), .mode("unsigned")) comparator_8 (.a(Opcode), .b(7'b0110011), .eq(rop1));  // open: gt, lt
  Comparator #(.width(7), .mode("unsigned")) comparator_9 (.a(Funct7), .b({7{1'b0}}), .eq(_00func7));  // open: gt, lt
  Comparator #(.width(7), .mode("unsigned")) comparator_10 (.a(Funct7), .b(7'b0000001), .eq(_01func7));  // open: gt, lt
  Comparator #(.width(7), .mode("unsigned")) comparator_11 (.a(Funct7), .b(7'b0100000), .eq(_20func7));  // open: gt, lt
  or or_1 (ITYPE, iop03, iop67, iop13);
  Comparator #(.width(7)) comparator_12 (.a(Opcode), .b(7'b0100011), .eq(MemRW));  // open: gt, lt
  or or_2 (RegWEn, rop1, ITYPE, uop, ujop);
  Comparator #(.width(3), .mode("unsigned")) comparator_13 (
    .a(Funct3), .b(3'b000), .eq(comparator_13_eq));  // open: gt, lt
  Comparator #(.width(3), .mode("unsigned")) comparator_14 (
    .a(Funct3), .b(3'b101), .eq(comparator_14_eq));  // open: gt, lt
  Comparator #(.width(3), .mode("unsigned")) comparator_15 (
    .a(Funct3), .b(3'b110), .eq(comparator_15_eq));  // open: gt, lt
  Comparator #(.width(3), .mode("unsigned")) comparator_16 (
    .a(Funct3), .b(3'b000), .eq(comparator_16_eq));  // open: gt, lt
  Comparator #(.width(3), .mode("unsigned")) comparator_17 (
    .a(Funct3), .b(3'b001), .eq(comparator_17_eq));  // open: gt, lt
  Comparator #(.width(3), .mode("unsigned")) comparator_18 (
    .a(Funct3), .b(3'b101), .eq(comparator_18_eq));  // open: gt, lt
  Comparator #(.width(3), .mode("unsigned")) comparator_19 (
    .a(Funct3), .b(3'b010), .eq(comparator_19_eq));  // open: gt, lt
  Comparator #(.width(3), .mode("unsigned")) comparator_20 (
    .a(Funct3), .b(3'b010), .eq(comparator_20_eq));  // open: gt, lt
  Comparator #(.width(3), .mode("unsigned")) comparator_21 (
    .a(Funct3), .b(3'b110), .eq(comparator_21_eq));  // open: gt, lt
  and and_1 (and_1_out, BrEq, isBranch, BEQ);
  and and_2 (and_2_out, BrLt, isBranch, BLT);
  Comparator #(.width(3), .mode("unsigned")) comparator_22 (
    .a(Funct3), .b(3'b111), .eq(comparator_22_eq));  // open: gt, lt
  Comparator #(.width(3), .mode("unsigned")) comparator_23 (
    .a(Funct3), .b(3'b010), .eq(comparator_23_eq));  // open: gt, lt
  Comparator #(.width(3), .mode("unsigned")) comparator_24 (
    .a(Funct3), .b(3'b000), .eq(comparator_24_eq));  // open: gt, lt
  Comparator #(.width(3), .mode("unsigned")) comparator_25 (
    .a(Funct3), .b(3'b000), .eq(comparator_25_eq));  // open: gt, lt
  and and_3 (and_3_out, comparator_13_eq, _20func7);
  and and_4 (and_4_out, comparator_14_eq, _00func7);
  and and_5 (and_5_out, comparator_15_eq, _01func7);
  and and_6 (ADDI, iop13, comparator_16_eq);
  and and_7 (and_7_out, comparator_17_eq, _00func7);
  and and_8 (and_8_out, comparator_18_eq, _00func7);
  and and_9 (SW, sop, comparator_19_eq);
  and and_10 (BEQ, sbop, comparator_20_eq);
  and and_11 (BLTU, sbop, comparator_21_eq);
  or or_3 (or_3_out, rop1, sop, sbop);
  not not_1 (BSel, or_3_out);
  or or_4 (PCSel, and_1_out, and_2_out, isJump);
  and and_12 (AND, rop1, comparator_22_eq);
  and and_13 (SLT, rop1, comparator_23_eq);
  and and_14 (ADD, rop1, and_15_out);
  and and_15 (and_15_out, comparator_24_eq, _00func7);
  and and_16 (MUL, rop1, and_17_out);
  and and_17 (and_17_out, comparator_25_eq, _01func7);
  and and_18 (SUB, rop1, and_3_out);
  and and_19 (SRL, rop1, and_4_out);
  and and_20 (REM, rop1, and_5_out);
  and and_21 (SLLI, iop13, and_7_out);
  and and_22 (SRLI, iop13, and_8_out);
  Comparator #(.width(3), .mode("unsigned")) comparator_26 (
    .a(Funct3), .b(3'b000), .eq(comparator_26_eq));  // open: gt, lt
  or or_5 (isBranch, BEQ, BLT, BLTU);
  Comparator #(.width(3), .mode("unsigned")) comparator_27 (
    .a(Funct3), .b(3'b001), .eq(comparator_27_eq));  // open: gt, lt
  Comparator #(.width(3), .mode("unsigned")) comparator_28 (
    .a(Funct3), .b(3'b001), .eq(comparator_28_eq));  // open: gt, lt
  Comparator #(.width(3), .mode("unsigned")) comparator_29 (
    .a(Funct3), .b(3'b100), .eq(comparator_29_eq));  // open: gt, lt
  Comparator #(.width(3), .mode("unsigned")) comparator_30 (
    .a(Funct3), .b(3'b100), .eq(comparator_30_eq));  // open: gt, lt
  Comparator #(.width(3), .mode("unsigned")) comparator_31 (
    .a(Funct3), .b(3'b110), .eq(comparator_31_eq));  // open: gt, lt
  Comparator #(.width(3), .mode("unsigned")) comparator_32 (
    .a(Funct3), .b(3'b000), .eq(comparator_32_eq));  // open: gt, lt
  Comparator #(.width(3), .mode("unsigned")) comparator_33 (
    .a(Funct3), .b(3'b001), .eq(comparator_33_eq));  // open: gt, lt
  Comparator #(.width(3), .mode("unsigned")) comparator_34 (
    .a(Funct3), .b(3'b010), .eq(comparator_34_eq));  // open: gt, lt
  Comparator #(.width(3), .mode("unsigned")) comparator_35 (
    .a(Funct3), .b(3'b100), .eq(comparator_35_eq));  // open: gt, lt
  Comparator #(.width(3), .mode("unsigned")) comparator_36 (
    .a(Funct3), .b(3'b110), .eq(comparator_36_eq));  // open: gt, lt
  Comparator #(.width(3), .mode("unsigned")) comparator_37 (
    .a(Funct3), .b(3'b111), .eq(comparator_37_eq));  // open: gt, lt
  Comparator #(.width(3), .mode("unsigned")) comparator_38 (
    .a(Funct3), .b(3'b100), .eq(comparator_38_eq));  // open: gt, lt
  and and_23 (JALR, iop67, comparator_26_eq);
  or or_6 (ASel, isBranch, isJump);
  and and_24 (and_24_out, comparator_27_eq, _00func7);
  and and_25 (and_25_out, comparator_28_eq, _01func7);
  and and_26 (and_26_out, comparator_29_eq, _00func7);
  and and_27 (and_27_out, comparator_30_eq, _01func7);
  and and_28 (and_28_out, comparator_31_eq, _00func7);
  and and_29 (LB, iop03, comparator_32_eq);
  and and_30 (LH, iop03, comparator_33_eq);
  Comparator #(.width(3), .mode("unsigned")) comparator_39 (
    .a(Funct3), .b(3'b010), .eq(comparator_39_eq));  // open: gt, lt
  and and_31 (SLTI, iop13, comparator_34_eq);
  and and_32 (XORI, iop13, comparator_35_eq);
  and and_33 (ORI, iop13, comparator_36_eq);
  and and_34 (ANDI, iop13, comparator_37_eq);
  and and_35 (BLT, sbop, comparator_38_eq);
  and and_36 (SLL, rop1, and_24_out);
  and and_37 (MULH, rop1, and_25_out);
  and and_38 (XOR, rop1, and_26_out);
  and and_39 (DIV, rop1, and_27_out);
  and and_40 (OR, rop1, and_28_out);
  and and_41 (LW, iop03, comparator_39_eq);
  or or_7 (isJump, ujop, JALR);

  // Other names for the same wires on the sheet: BrUn = BLTU; func3[2:0] = Funct3; func7[6:0] = Funct7;
  //   op[6:0] = Opcode; RTYPE = rop1; SBTYPE = sbop; STYPE = sop; UJTYPE = ujop; UTYPE = uop
endmodule
